# Fritzing sketch ART (saved by Fritzing 0.4.3b)

parts:
  IC1 = DIP - 40 pins
  IFH = Generic female header - 3 pins [package=THT]
  UFH = Generic female header - 4 pins [package=THT]
  RFH2 = Generic female header - 9 pins [package=THT]
  RFH1 = Generic female header - 9 pins [package=THT]
  Infrared_Forward = Infrared Proximity Sensor
  Arduino_Uno = Arduino
  IRH = Generic female header - 3 pins [package=THT]
  URH = Generic female header - 4 pins [package=THT]
  Infrared_Right = Infrared Proximity Sensor
  MH = Generic female header - 4 pins [package=THT]
  IBH = Generic female header - 3 pins [package=THT]
  UBH = Generic female header - 4 pins [package=THT]
  Infrared_Backward = Infrared Proximity Sensor
  ILH = Generic female header - 3 pins [package=THT]
  ULH = Generic female header - 4 pins [package=THT]
  Infrared_Left = Infrared Proximity Sensor
  Ultrasonic_Forward = SRF05 Ultrasonic Rangefinder
  Ultrasonic_Left = SRF05 Ultrasonic Rangefinder
  Ultrasonic_Right = SRF05 Ultrasonic Rangefinder
  Ultrasonic_Backward = SRF05 Ultrasonic Rangefinder

nets:
  N1: IC1.connector0, Arduino_Uno.D2
  N2: IC1.connector1, Arduino_Uno.D3
  N3: IC1.connector2, Arduino_Uno.D4
  N4: IC1.connector3, Arduino_Uno.D5
  N5: IC1.connector8, Arduino_Uno.D6
  N6: IC1.connector9, Arduino_Uno.D7
  N7: IC1.connector10, ULH.pin3, Ultrasonic_Left.connector9
  N8: IC1.connector11, ULH.pin2, Ultrasonic_Left.connector10
  N9: IC1.connector12, Arduino_Uno.D8
  N10: IC1.connector13, Arduino_Uno.D9
  N11: IC1.connector15, ILH.pin3, Infrared_Left.Vout
  N12: IC1.connector16, IBH.pin3, Infrared_Backward.Vout
  N13: IC1.connector21, MH.pin4
  N14: IC1.connector22, MH.pin3
  N15: IC1.connector23, MH.pin2
  N16: IC1.connector24, MH.pin1
  N17: IC1.connector25, UBH.pin3, Ultrasonic_Backward.connector9
  N18: IC1.connector26, UBH.pin2, Ultrasonic_Backward.connector10
  N19: IC1.connector27, IRH.pin3, Infrared_Right.Vout
  N20: IC1.connector31, URH.pin3, Ultrasonic_Right.connector9
  N21: IC1.connector32, URH.pin2, Ultrasonic_Right.connector10
  N22: IC1.connector33, IFH.pin3, Infrared_Forward.Vout
  N23: IC1.connector35, UFH.pin2, Ultrasonic_Forward.connector10
  N24: IC1.connector36, UFH.pin3, Ultrasonic_Forward.connector9
  N25: IC1.connector37, Arduino_Uno.A1
  N26: IC1.connector38, Arduino_Uno.A2
  N27: IC1.connector39, Arduino_Uno.A3
  VCC: IFH.pin1, UFH.pin4, RFH2.pin9, RFH1.pin1, RFH1.pin2, Infrared_Forward.Vcc, Arduino_Uno.+5V, IRH.pin1, URH.pin4, Infrared_Right.Vcc, ILH.pin1, ULH.pin4, Infrared_Left.Vcc, Ultrasonic_Forward.connector8, Ultrasonic_Left.connector8, Ultrasonic_Right.connector8
  GND: IFH.pin2, UFH.pin1, RFH2.pin1, RFH2.pin2, Infrared_Forward.GND, Arduino_Uno.GND, IRH.pin2, URH.pin1, Infrared_Right.GND, IBH.pin2, Infrared_Backward.GND, ILH.pin2, ULH.pin1, Infrared_Left.GND, Ultrasonic_Forward.connector11, Ultrasonic_Left.connector11, Ultrasonic_Right.connector11
  N28: RFH2.pin3, Arduino_Uno.D11
  N29: RFH2.pin4, RFH2.pin5, Arduino_Uno.D10
  N30: RFH1.pin4, RFH1.pin5, Arduino_Uno.D12
  N31: RFH1.pin6, RFH1.pin7, Arduino_Uno.D13
  N32: IBH.pin1, Infrared_Backward.Vcc
  N33: UBH.pin1, Ultrasonic_Backward.connector11
  N34: UBH.pin4, Ultrasonic_Backward.connector8
